// Logisim project Weird_CPU_v1.circ as structural Verilog: 1 circuit, main circuit Weird_CPU
module Weird_CPU (
);

  wire A_WR, A_WR_ENABLE, adder_1_cout, ADDR_SEL, and_1_out, and_2_out, and_3_out, and_4_out, and_5_out,
       and_6_out, and_7_out, CLK, comparator_1_eq, comparator_2_eq, comparator_3_eq, Cout, DATAMEM, HALT,
       IOMEM, MWR, not_2_out, not_3_out, not_4_out, not_5_out, or_1_out, P_JMP, P_UPDATE, RD_EA, RD_I, RST;
  wire [1:0] ALU_MUX, CONTROL_CTR_q;
  wire [7:0] A_q, adder_1_out, adder_2_out, ADDR, CONTROL_STORE_data, DATA, EA_q, I, keyboard_1_data,
       multiplexer_1_out, multiplexer_2_out, nand_1_out, not_1_out, P_q, register_2_q;

  Button button_1 (.out(RST));
  Clock clock_1 (.out(CLK));
  Counter #(.max('h3), .width(2)) CONTROL_CTR (
    .clr(RST), .load(1'b0), .up(1'b1), .count(1'b1), .clk(CLK), .Q(CONTROL_CTR_q));  // open: D, carry
  Register register_1 (.D(DATA), .en(RD_I), .clk(CLK), .Q({I[7], HALT, I[5:4], ALU_MUX, A_WR_ENABLE, I[0]}), .clr(RST));
  and and_1 (and_1_out, MWR, IOMEM, comparator_1_eq);
  Comparator #(.mode("unsigned")) comparator_1 (.a(ADDR), .b({8{1'b1}}), .eq(comparator_1_eq));  // open: gt, lt
  ROM #(.addrWidth(2)) CONTROL_STORE (
    .addr(CONTROL_CTR_q), .data({CONTROL_STORE_data[7], RD_I, RD_EA, ADDR_SEL, CONTROL_STORE_data[3:0]}));
  Register register_2 (.D(DATA), .en(and_1_out), .clk(CLK), .Q(register_2_q), .clr(RST));
  Adder adder_1 (.a(A_q), .b(DATA), .out(adder_1_out), .cout(adder_1_cout));  // open: cin
  assign nand_1_out = ~(DATA & A_q);  // NAND_Gate nand_1, 8 bits wide
  assign not_1_out = ~DATA;  // NOT_Gate not_1, 8 bits wide
  Adder adder_2 (.a(P_q), .b(8'h1), .out(adder_2_out), .cin(1'b0));  // open: cout
  Multiplexer #(.enable("false"), .width(8)) multiplexer_1 (
    .in0(adder_2_out), .in1(DATA), .out(multiplexer_1_out), .sel(P_JMP));
  Hex_Digit_Display hex_digit_display_1 (.value(register_2_q[7:4]));  // open: dp
  Register EA (.D(DATA), .en(RD_EA), .clk(CLK), .Q(EA_q), .clr(RST));
  Register P (.D(multiplexer_1_out), .en(P_UPDATE), .clk(CLK), .Q(P_q), .clr(RST));
  Hex_Digit_Display hex_digit_display_2 (.value(register_2_q[3:0]));  // open: dp
  Register A (.D(multiplexer_2_out), .en(A_WR), .clk(CLK), .Q(A_q), .clr(RST));
  Multiplexer #(.enable("false"), .select(2), .width(8)) multiplexer_2 (
    .in0(DATA), .in1(adder_1_out), .in2(nand_1_out), .in3(not_1_out), .out(multiplexer_2_out), .sel(ALU_MUX));
  Multiplexer #(.enable("false"), .width(8)) multiplexer_3 (.in0(EA_q), .in1(P_q), .out(ADDR), .sel(ADDR_SEL));
  Comparator #(.mode("unsigned")) comparator_2 (.a(ADDR), .b({8{1'b1}}), .eq(comparator_2_eq));  // open: gt, lt
  assign DATA = MWR ? A_q : 8'bz;  // Controlled_Buffer controlled_buffer_1
  not not_2 (not_2_out, Cout);
  and and_2 (and_2_out, MWR, IOMEM, comparator_2_eq);
  not not_3 (not_3_out, MWR);
  Comparator #(.mode("unsigned")) comparator_3 (.a(ADDR), .b(8'hfe), .eq(comparator_3_eq));  // open: gt, lt
  Register #(.width(1)) C (.D(adder_1_cout), .en(A_WR), .clk(CLK), .Q(Cout), .clr(RST));
  not not_4 (not_4_out, MWR);
  or or_1 (or_1_out, I[4], not_2_out);
  TTY tty_1 (.data(DATA[6:0]), .clk(CLK), .we(and_2_out), .clr(and_3_out));
  and and_3 (and_3_out, and_2_out, DATA[7]);
  Keyboard keyboard_1 (
    .clk(CLK), .re(and_4_out), .avail(keyboard_1_data[7]), .data(keyboard_1_data[6:0]));  // open: clr
  and and_4 (and_4_out, not_3_out, A_WR, IOMEM, comparator_3_eq);
  RAM #(.asyncread("true"), .databus("bidir"), .\type ("nonvolatile")) MEM (
    .addr(ADDR), .we(and_5_out), .oe(and_6_out), .clk(CLK), .data(DATA));
  and and_5 (and_5_out, DATAMEM, MWR);
  and and_6 (and_6_out, not_4_out, DATAMEM);
  not not_5 (not_5_out, HALT);
  and and_7 (and_7_out, CONTROL_STORE_data[2], I[5]);
  assign DATA = and_4_out ? keyboard_1_data : 8'bz;  // Controlled_Buffer controlled_buffer_2
  and and_8 (IOMEM, I[7], CONTROL_STORE_data[7]);
  and and_9 (P_UPDATE, CONTROL_STORE_data[3], not_5_out);
  and and_10 (P_JMP, or_1_out, and_7_out);
  and and_11 (A_WR, CONTROL_STORE_data[1], A_WR_ENABLE);
  and and_12 (MWR, CONTROL_STORE_data[0], I[0]);
  not not_6 (DATAMEM, IOMEM);
  Pull_Resistor #(.pull(1)) pull_resistor_1 (.node(DATA));

  // Other names for the same wires on the sheet: MWR_ENABLE = I[0]; I (some bits) = {HALT, ALU_MUX, A_WR_ENABLE};
  //   JMP_CONDITION = I[4]; JMP_ENABLE = I[5]; IO_SW = I[7]

  // Notes on the sheet:
  //   contents of CONTROL_STORE (hex, n*v repeats v):
  //   58 3c 82 81
endmodule
